# Fritzing sketch NodeMCU_ve_3D_Yazici_Ile_RC_Tank_Yapimi_Devre_Semasi (saved by Fritzing 0.9.3b)

parts:
  M1 = BTS7960
  M2 = BTS7960
  U3 = LIPO-2000mAh [package=lipo-2000]
  M3 = DC Motor
  M4 = DC Motor
  U4 = NodeMCU V3.0
  Mod1 = flyskyr6b
  J1 = Basic Servo
  J2 = Basic Servo
  VCC1 = 4 x AAA Battery Mount

nets:
  N1: M1.pin1, U4.D1
  N2: M1.pin2, U4.D0
  N3: M1.pin3, M1.pin4, U4.D2
  N4: M1.pin7, U4.VU
  GND: M1.pin8, M2.pin7, M2.pin8, U4.GND, Mod1.connector14, Mod1.GND, J1.gnd, J2.gnd, VCC1.-
  N5: M1.pin9, M4.pin_2
  N6: M1.pin10, M4.pin_1
  N7: M1.pin11, M2.pin11, U3.+
  N8: M1.pin12, M2.pin12, U3.-
  N9: M2.pin1, U4.D4
  N10: M2.pin2, U4.D3
  N11: M2.pin3, U4.D7
  N12: M2.pin9, M3.pin_2
  N13: M2.pin10, M3.pin_1
  N14: U4.D5, Mod1.CH2
  N15: U4.D6, Mod1.CH3
  N16: U4.Vin, VCC1.+
  N17: Mod1.CH5, J2.pulse
  N18: Mod1.CH6, J1.pulse
  VCC: Mod1.VCC, Mod1.BAT+, J1.vcc, J2.vcc

custom parts:
  BTS7960: BTS7960 43A Peak Power H-Bridge PWM Motor Driver
  NodeMCU V3.0: ESP8266 based NodeMCU
  flyskyr6b: flysky r6b 6ch rc receiver module. Pcb view is 3*7 header pins, 3 female headers will let the board plug in to the receiver, or connect via wires as you choose.
